// Logisim project ADDERS.circ as structural Verilog
module FULL_ADDER (
  input  A,
  input  B,
  input  Cin,
  output S,
  output Cout
);

  wire and_1_out, and_2_out, xor_1_out;

  xor xor_1 (xor_1_out, A, B);
  xor xor_2 (S, xor_1_out, Cin);
  and and_1 (and_1_out, xor_1_out, Cin);
  and and_2 (and_2_out, A, B);
  or or_1 (Cout, and_1_out, and_2_out);
endmodule

module Ripple_Carry_Adder (
  input  B3,
  input  A3,
  input  B2,
  input  A2,
  input  B1,
  input  A1,
  input  B0,
  input  A0,
  input  Cin,
  output Cout,
  output S3,
  output S2,
  output S1,
  output S0
);

  wire full_adder_2_cout, full_adder_3_cout, full_adder_4_cout;

  FULL_ADDER full_adder_1 (.A(A3), .B(B3), .Cin(full_adder_2_cout), .S(S3), .Cout(Cout));
  FULL_ADDER full_adder_2 (.A(A2), .B(B2), .Cin(full_adder_3_cout), .S(S2), .Cout(full_adder_2_cout));
  FULL_ADDER full_adder_3 (.A(A1), .B(B1), .Cin(full_adder_4_cout), .S(S1), .Cout(full_adder_3_cout));
  FULL_ADDER full_adder_4 (.A(A0), .B(B0), .Cin(Cin), .S(S0), .Cout(full_adder_4_cout));
endmodule

module FULL_ADDER2 (
  input  A,
  input  B,
  input  Cin,
  output P,
  output G,
  output S
);

  wire and_1_out, or_1_out;

  xor xor_1 (P, A, B);
  xor xor_2 (S, P, Cin);
  and and_1 (and_1_out, P, Cin);
  and and_2 (G, A, B);
  or or_1 (or_1_out, and_1_out, G);
endmodule

module CLA_Carrie (
  input  G3,
  input  P3,
  input  G2,
  input  P2,
  input  G1,
  input  P1,
  input  G0,
  input  P0,
  input  Cin,
  output C3,
  output C2,
  output C1,
  output C0
);

  wire and_1_out, and_2_out, and_3_out, and_4_out, and_5_out, and_6_out, and_7_out, and_8_out, and_9_out,
       and_10_out;

  and and_1 (and_1_out, P0, Cin);
  and and_2 (and_2_out, Cin, P0, P1, P2, P3);
  and and_3 (and_3_out, G0, P1, P2, P3);
  and and_4 (and_4_out, G1, P2, P3);
  and and_5 (and_5_out, G2, P3);
  and and_6 (and_6_out, Cin, P0, P1, P2);
  and and_7 (and_7_out, G0, P1, P2);
  and and_8 (and_8_out, G1, P2);
  and and_9 (and_9_out, P1, G0, Cin);
  and and_10 (and_10_out, P1, G0);
  or or_1 (C0, G0, and_1_out);
  or or_2 (C3, and_2_out, and_3_out, and_4_out, and_5_out, G3);
  or or_3 (C2, and_6_out, and_7_out, and_8_out, G2);
  or or_4 (C1, and_9_out, G1, and_10_out);
endmodule

module CARRY_LOOKAHEAD (
  input  B3,
  input  A3,
  input  B2,
  input  A2,
  input  B1,
  input  A1,
  input  B0,
  input  A0,
  input  Cin,
  output Cout,
  output S3,
  output S2,
  output S1,
  output S0
);

  wire C0, C1, C2, G0, G1, G2, G3, P0, P1, P2, P3;

  FULL_ADDER2 full_adder2_1 (.A(A3), .B(B3), .Cin(C2), .P(P3), .G(G3), .S(S3));
  FULL_ADDER2 full_adder2_2 (.A(A2), .B(B2), .Cin(C1), .P(P2), .G(G2), .S(S2));
  FULL_ADDER2 full_adder2_3 (.A(A1), .B(B1), .Cin(C0), .P(P1), .G(G1), .S(S1));
  CLA_Carrie cla_carrie_1 (
    .G3(G3), .P3(P3), .G2(G2), .P2(P2), .G1(G1), .P1(P1), .G0(G0), .P0(P0), .Cin(Cin), .C3(Cout), .C2(C2),
    .C1(C1), .C0(C0));
  FULL_ADDER2 full_adder2_4 (.A(A0), .B(B0), .Cin(Cin), .P(P0), .G(G0), .S(S0));

  // Other names for the same wires on the sheet: C3 = Cout
endmodule

module P_G (
  input  A0,
  input  B0,
  input  A1,
  input  B1,
  input  A2,
  input  B2,
  input  A3,
  input  B3,
  output P0,
  output G0,
  output P1,
  output G1,
  output P2,
  output G2,
  output P3,
  output G3
);

  or or_1 (P0, A0, B0);
  and and_1 (G0, A0, B0);
  or or_2 (P1, A1, B1);
  and and_2 (G1, A1, B1);
  or or_3 (P2, A2, B2);
  and and_3 (G2, A2, B2);
  or or_4 (P3, A3, B3);
  and and_4 (G3, A3, B3);
endmodule

module PREFIX_LEVEL (
  input  Cin,
  input  P0,
  input  G0,
  input  P1,
  input  G1,
  input  P2,
  input  G2,
  input  P3,
  input  G3,
  output G_out0,
  output G_out1,
  output G_out2,
  output G_out3,
  output Cout
);

  wire and_1_out, and_2_out, and_3_out, and_4_out, and_5_out, and_6_out, or_2_out;

  and and_1 (and_1_out, Cin, P0);
  and and_2 (and_2_out, G1, P2);
  and and_3 (and_3_out, P1, P2);
  or or_1 (G_out1, and_1_out, G0);
  or or_2 (or_2_out, and_2_out, G2);
  and and_4 (and_4_out, G_out1, P1);
  and and_5 (and_5_out, G_out1, and_3_out);
  or or_3 (G_out2, and_4_out, G1);
  or or_4 (G_out3, and_5_out, or_2_out);
  and and_6 (and_6_out, G_out3, P3);
  or or_5 (Cout, and_6_out, G3);

  assign G_out0 = Cin;
endmodule

module PREFIX_S (
  input  A0,
  input  B0,
  input  G_out0,
  input  A1,
  input  B1,
  input  G_out1,
  input  A2,
  input  B2,
  input  G_out2,
  input  A3,
  input  B3,
  input  G_out3,
  output S0,
  output S1,
  output S2,
  output S3
);

  wire xor_1_out, xor_2_out, xor_3_out, xor_4_out;

  xor xor_1 (xor_1_out, A0, B0);
  xor xor_2 (xor_2_out, A1, B1);
  xor xor_3 (xor_3_out, A2, B2);
  xor xor_4 (xor_4_out, A3, B3);
  xor xor_5 (S0, xor_1_out, G_out0);
  xor xor_6 (S1, xor_2_out, G_out1);
  xor xor_7 (S2, xor_3_out, G_out2);
  xor xor_8 (S3, xor_4_out, G_out3);
endmodule

module PREFIX_ADDER (
  input  Cin,
  input  B3,
  input  A3,
  input  B2,
  input  A2,
  input  B1,
  input  A1,
  input  B0,
  input  A0,
  output Cout,
  output S3,
  output S2,
  output S1,
  output S0
);

  wire G0, G1, G2, G3, GO0, GO1, GO2, GO3, P0, P1, P2, P3;

  P_G p_g_1 (
    .A0(A0), .B0(B0), .A1(A1), .B1(B1), .A2(A2), .B2(B2), .A3(A3), .B3(B3), .P0(P0), .G0(G0), .P1(P1),
    .G1(G1), .P2(P2), .G2(G2), .P3(P3), .G3(G3));
  PREFIX_LEVEL prefix_level_1 (
    .Cin(Cin), .P0(P0), .G0(G0), .P1(P1), .G1(G1), .P2(P2), .G2(G2), .P3(P3), .G3(G3), .G_out0(GO0),
    .G_out1(GO1), .G_out2(GO2), .G_out3(GO3), .Cout(Cout));
  PREFIX_S prefix_s_1 (
    .A0(A0), .B0(B0), .G_out0(GO0), .A1(A1), .B1(B1), .G_out1(GO1), .A2(A2), .B2(B2), .G_out2(GO2), .A3(A3),
    .B3(B3), .G_out3(GO3), .S0(S0), .S1(S1), .S2(S2), .S3(S3));
endmodule
