// Logisim project ALUcontrol.circ as structural Verilog: 9 circuits, main circuit main
module main (
  input  [2:0] ALU_CONTROL,
  input  [3:0] BITS_IZQUIERDA,
  input  [9:0] A,
  input  [3:0] BITS_DERECHA,
  input  [9:0] B,
  output [9:0] RESULTADO,
  output [3:0] ALU_FLAGS
);

  wire Cout;
  wire [9:0] AandB, AorB, DERECHA, IZQUIERDA, SUM_REST;

  Multiplexer #(.select(3), .width(10)) multiplexer_1 (
    .in0(SUM_REST), .in1(SUM_REST), .in2(AandB), .in3(AorB), .in4(IZQUIERDA), .in5(IZQUIERDA), .in6(DERECHA),
    .in7(DERECHA), .out(RESULTADO), .sel(ALU_CONTROL));
  ALUFLAGS aluflags_1 (
    .Cout(Cout), .ALU_CONTROL(ALU_CONTROL), .SUMARESTA9(SUM_REST[9]), .A9(A[9]), .B9(B[9]),
    .RESULTADO(RESULTADO), .FLAGS(ALU_FLAGS));
  LED OVERFLOW (.in(ALU_FLAGS[0]));
  LED CARRY (.in(ALU_FLAGS[1]));
  LED CERO (.in(ALU_FLAGS[2]));
  LED NEGATIVO (.in(ALU_FLAGS[3]));
  SUMA_RESTA suma_resta_1 (.ALU0(ALU_CONTROL[0]), .A(A), .B(B), .SUM_REST(SUM_REST), .Cout(Cout));
  ALU_AND alu_and_1 (.A(A), .B(B), .AandB(AandB));
  ALU_OR alu_or_1 (.A(A), .B(B), .AorB(AorB));
  MOVER_IZQUIERDA mover_izquierda_1 (.SUM_REST(SUM_REST), .shiftL(BITS_IZQUIERDA), .IZQUIERDA(IZQUIERDA));
  MOVER_DERECHA mover_derecha_1 (.SUM_REST(SUM_REST), .shiftR(BITS_DERECHA), .DERECHA(DERECHA));

  // Other names for the same wires on the sheet: ALU_F[3:0] = ALU_FLAGS; ALU0 = ALU_CONTROL[0];
  //   ALUC[2:0] = ALU_CONTROL; RESP[9:0] = RESULTADO; SHIFT_L[3:0] = BITS_IZQUIERDA; SHIFT_R[3:0] = BITS_DERECHA
endmodule

module FULL_ADD (
  input  A,
  input  B,
  input  Cin,
  output S,
  output Cout
);

  wire and_1_out, and_2_out, xor_1_out;

  xor xor_1 (xor_1_out, A, B);
  xor xor_2 (S, xor_1_out, Cin);
  and and_1 (and_1_out, xor_1_out, Cin);
  and and_2 (and_2_out, A, B);
  or or_1 (Cout, and_1_out, and_2_out);
endmodule

module R_ADDER (
  input  [9:0] A,
  input  [9:0] B,
  input  Cin,
  output [9:0] S,
  output Cout
);

  wire full_add_1_cout, full_add_2_cout, full_add_3_cout, full_add_4_cout, full_add_5_cout, full_add_6_cout,
       full_add_7_cout, full_add_8_cout, full_add_9_cout;

  FULL_ADD full_add_1 (.A(A[0]), .B(B[0]), .Cin(Cin), .S(S[0]), .Cout(full_add_1_cout));
  FULL_ADD full_add_2 (.A(A[1]), .B(B[1]), .Cin(full_add_1_cout), .S(S[1]), .Cout(full_add_2_cout));
  FULL_ADD full_add_3 (.A(A[2]), .B(B[2]), .Cin(full_add_2_cout), .S(S[2]), .Cout(full_add_3_cout));
  FULL_ADD full_add_4 (.A(A[3]), .B(B[3]), .Cin(full_add_3_cout), .S(S[3]), .Cout(full_add_4_cout));
  FULL_ADD full_add_5 (.A(A[4]), .B(B[4]), .Cin(full_add_4_cout), .S(S[4]), .Cout(full_add_5_cout));
  FULL_ADD full_add_6 (.A(A[5]), .B(B[5]), .Cin(full_add_5_cout), .S(S[5]), .Cout(full_add_6_cout));
  FULL_ADD full_add_7 (.A(A[6]), .B(B[6]), .Cin(full_add_6_cout), .S(S[6]), .Cout(full_add_7_cout));
  FULL_ADD full_add_8 (.A(A[7]), .B(B[7]), .Cin(full_add_7_cout), .S(S[7]), .Cout(full_add_8_cout));
  FULL_ADD full_add_9 (.A(A[8]), .B(B[8]), .Cin(full_add_8_cout), .S(S[8]), .Cout(full_add_9_cout));
  FULL_ADD full_add_10 (.A(A[9]), .B(B[9]), .Cin(full_add_9_cout), .S(S[9]), .Cout(Cout));

  // Other names for the same wires on the sheet: ALU0 = Cin
endmodule

module SUMA_RESTA (
  input  ALU0,
  input  [9:0] A,
  input  [9:0] B,
  output [9:0] SUM_REST,
  output Cout
);

  wire [9:0] multiplexer_1_out, not_1_out;

  assign not_1_out = ~B;  // NOT_Gate not_1, 10 bits wide
  Multiplexer #(.width(10)) multiplexer_1 (.in0(B), .in1(not_1_out), .out(multiplexer_1_out), .sel(ALU0));
  R_ADDER r_adder_1 (.A(A), .B(multiplexer_1_out), .Cin(ALU0), .S(SUM_REST), .Cout(Cout));
endmodule

module ALU_AND (
  input  [9:0] A,
  input  [9:0] B,
  output [9:0] AandB
);

  assign AandB = A & B;  // AND_Gate and_1, 10 bits wide
endmodule

module ALU_OR (
  input  [9:0] A,
  input  [9:0] B,
  output [9:0] AorB
);

  assign AorB = A | B;  // OR_Gate or_1, 10 bits wide
endmodule

module MOVER_IZQUIERDA (
  input  [9:0] SUM_REST,
  input  [3:0] shiftL,
  output [9:0] IZQUIERDA
);

  Multiplexer #(.select(4)) multiplexer_1 (
    .in0(SUM_REST[9]), .in1(SUM_REST[8]), .in2(SUM_REST[7]), .in3(SUM_REST[6]), .in4(SUM_REST[5]),
    .in5(SUM_REST[4]), .in6(SUM_REST[3]), .in7(SUM_REST[2]), .in8(SUM_REST[1]), .in9(SUM_REST[0]),
    .in10(1'b0), .in11(1'b0), .in12(1'b0), .in13(1'b0), .in14(1'b0), .in15(1'b0), .out(IZQUIERDA[9]),
    .sel(shiftL));
  Multiplexer #(.select(4)) multiplexer_2 (
    .in0(SUM_REST[8]), .in1(SUM_REST[7]), .in2(SUM_REST[6]), .in3(SUM_REST[5]), .in4(SUM_REST[4]),
    .in5(SUM_REST[3]), .in6(SUM_REST[2]), .in7(SUM_REST[1]), .in8(SUM_REST[0]), .in9(1'b0), .in10(1'b0),
    .in11(1'b0), .in12(1'b0), .in13(1'b0), .in14(1'b0), .in15(1'b0), .out(IZQUIERDA[8]), .sel(shiftL));
  Multiplexer #(.select(4)) multiplexer_3 (
    .in0(SUM_REST[7]), .in1(SUM_REST[6]), .in2(SUM_REST[5]), .in3(SUM_REST[4]), .in4(SUM_REST[3]),
    .in5(SUM_REST[2]), .in6(SUM_REST[1]), .in7(SUM_REST[0]), .in8(1'b0), .in9(1'b0), .in10(1'b0),
    .in11(1'b0), .in12(1'b0), .in13(1'b0), .in14(1'b0), .in15(1'b0), .out(IZQUIERDA[7]), .sel(shiftL));
  Multiplexer #(.select(4)) multiplexer_4 (
    .in0(SUM_REST[6]), .in1(SUM_REST[5]), .in2(SUM_REST[4]), .in3(SUM_REST[3]), .in4(SUM_REST[2]),
    .in5(SUM_REST[1]), .in6(SUM_REST[0]), .in7(1'b0), .in8(1'b0), .in9(1'b0), .in10(1'b0), .in11(1'b0),
    .in12(1'b0), .in13(1'b0), .in14(1'b0), .in15(1'b0), .out(IZQUIERDA[6]), .sel(shiftL));
  Multiplexer #(.select(4)) multiplexer_5 (
    .in0(SUM_REST[5]), .in1(SUM_REST[4]), .in2(SUM_REST[3]), .in3(SUM_REST[2]), .in4(SUM_REST[1]),
    .in5(SUM_REST[0]), .in6(1'b0), .in7(1'b0), .in8(1'b0), .in9(1'b0), .in10(1'b0), .in11(1'b0), .in12(1'b0),
    .in13(1'b0), .in14(1'b0), .in15(1'b0), .out(IZQUIERDA[5]), .sel(shiftL));
  Multiplexer #(.select(4)) multiplexer_6 (
    .in0(SUM_REST[4]), .in1(SUM_REST[3]), .in2(SUM_REST[2]), .in3(SUM_REST[1]), .in4(SUM_REST[0]),
    .in5(1'b0), .in6(1'b0), .in7(1'b0), .in8(1'b0), .in9(1'b0), .in10(1'b0), .in11(1'b0), .in12(1'b0),
    .in13(1'b0), .in14(1'b0), .in15(1'b0), .out(IZQUIERDA[4]), .sel(shiftL));
  Multiplexer #(.select(4)) multiplexer_7 (
    .in0(SUM_REST[3]), .in1(SUM_REST[2]), .in2(SUM_REST[1]), .in3(SUM_REST[0]), .in4(1'b0), .in5(1'b0),
    .in6(1'b0), .in7(1'b0), .in8(1'b0), .in9(1'b0), .in10(1'b0), .in11(1'b0), .in12(1'b0), .in13(1'b0),
    .in14(1'b0), .in15(1'b0), .out(IZQUIERDA[3]), .sel(shiftL));
  Multiplexer #(.select(4)) multiplexer_8 (
    .in0(SUM_REST[2]), .in1(SUM_REST[1]), .in2(SUM_REST[0]), .in3(1'b0), .in4(1'b0), .in5(1'b0), .in6(1'b0),
    .in7(1'b0), .in8(1'b0), .in9(1'b0), .in10(1'b0), .in11(1'b0), .in12(1'b0), .in13(1'b0), .in14(1'b0),
    .in15(1'b0), .out(IZQUIERDA[2]), .sel(shiftL));
  Multiplexer #(.select(4)) multiplexer_9 (
    .in0(SUM_REST[1]), .in1(SUM_REST[0]), .in2(1'b0), .in3(1'b0), .in4(1'b0), .in5(1'b0), .in6(1'b0),
    .in7(1'b0), .in8(1'b0), .in9(1'b0), .in10(1'b0), .in11(1'b0), .in12(1'b0), .in13(1'b0), .in14(1'b0),
    .in15(1'b0), .out(IZQUIERDA[1]), .sel(shiftL));
  Multiplexer #(.select(4)) multiplexer_10 (
    .in0(SUM_REST[0]), .in1(1'b0), .in2(1'b0), .in3(1'b0), .in4(1'b0), .in5(1'b0), .in6(1'b0), .in7(1'b0),
    .in8(1'b0), .in9(1'b0), .in10(1'b0), .in11(1'b0), .in12(1'b0), .in13(1'b0), .in14(1'b0), .in15(1'b0),
    .out(IZQUIERDA[0]), .sel(shiftL));
endmodule

module MOVER_DERECHA (
  input  [9:0] SUM_REST,
  input  [3:0] shiftR,
  output [9:0] DERECHA
);

  Multiplexer #(.select(4)) multiplexer_1 (
    .in0(SUM_REST[9]), .in1(1'b0), .in2(1'b0), .in3(1'b0), .in4(1'b0), .in5(1'b0), .in6(1'b0), .in7(1'b0),
    .in8(1'b0), .in9(1'b0), .in10(1'b0), .in11(1'b0), .in12(1'b0), .in13(1'b0), .in14(1'b0), .in15(1'b0),
    .out(DERECHA[9]), .sel(shiftR));
  Multiplexer #(.select(4)) multiplexer_2 (
    .in0(SUM_REST[8]), .in1(SUM_REST[9]), .in2(1'b0), .in3(1'b0), .in4(1'b0), .in5(1'b0), .in6(1'b0),
    .in7(1'b0), .in8(1'b0), .in9(1'b0), .in10(1'b0), .in11(1'b0), .in12(1'b0), .in13(1'b0), .in14(1'b0),
    .in15(1'b0), .out(DERECHA[8]), .sel(shiftR));
  Multiplexer #(.select(4)) multiplexer_3 (
    .in0(SUM_REST[7]), .in1(SUM_REST[8]), .in2(SUM_REST[9]), .in3(1'b0), .in4(1'b0), .in5(1'b0), .in6(1'b0),
    .in7(1'b0), .in8(1'b0), .in9(1'b0), .in10(1'b0), .in11(1'b0), .in12(1'b0), .in13(1'b0), .in14(1'b0),
    .in15(1'b0), .out(DERECHA[7]), .sel(shiftR));
  Multiplexer #(.select(4)) multiplexer_4 (
    .in0(SUM_REST[6]), .in1(SUM_REST[7]), .in2(SUM_REST[8]), .in3(SUM_REST[9]), .in4(1'b0), .in5(1'b0),
    .in6(1'b0), .in7(1'b0), .in8(1'b0), .in9(1'b0), .in10(1'b0), .in11(1'b0), .in12(1'b0), .in13(1'b0),
    .in14(1'b0), .in15(1'b0), .out(DERECHA[6]), .sel(shiftR));
  Multiplexer #(.select(4)) multiplexer_5 (
    .in0(SUM_REST[5]), .in1(SUM_REST[6]), .in2(SUM_REST[7]), .in3(SUM_REST[8]), .in4(SUM_REST[9]),
    .in5(1'b0), .in6(1'b0), .in7(1'b0), .in8(1'b0), .in9(1'b0), .in10(1'b0), .in11(1'b0), .in12(1'b0),
    .in13(1'b0), .in14(1'b0), .in15(1'b0), .out(DERECHA[5]), .sel(shiftR));
  Multiplexer #(.select(4)) multiplexer_6 (
    .in0(SUM_REST[4]), .in1(SUM_REST[5]), .in2(SUM_REST[6]), .in3(SUM_REST[7]), .in4(SUM_REST[8]),
    .in5(SUM_REST[9]), .in6(1'b0), .in7(1'b0), .in8(1'b0), .in9(1'b0), .in10(1'b0), .in11(1'b0), .in12(1'b0),
    .in13(1'b0), .in14(1'b0), .in15(1'b0), .out(DERECHA[4]), .sel(shiftR));
  Multiplexer #(.select(4)) multiplexer_7 (
    .in0(SUM_REST[3]), .in1(SUM_REST[4]), .in2(SUM_REST[5]), .in3(SUM_REST[6]), .in4(SUM_REST[7]),
    .in5(SUM_REST[8]), .in6(SUM_REST[9]), .in7(1'b0), .in8(1'b0), .in9(1'b0), .in10(1'b0), .in11(1'b0),
    .in12(1'b0), .in13(1'b0), .in14(1'b0), .in15(1'b0), .out(DERECHA[3]), .sel(shiftR));
  Multiplexer #(.select(4)) multiplexer_8 (
    .in0(SUM_REST[2]), .in1(SUM_REST[3]), .in2(SUM_REST[4]), .in3(SUM_REST[5]), .in4(SUM_REST[6]),
    .in5(SUM_REST[7]), .in6(SUM_REST[8]), .in7(SUM_REST[9]), .in8(1'b0), .in9(1'b0), .in10(1'b0),
    .in11(1'b0), .in12(1'b0), .in13(1'b0), .in14(1'b0), .in15(1'b0), .out(DERECHA[2]), .sel(shiftR));
  Multiplexer #(.select(4)) multiplexer_9 (
    .in0(SUM_REST[1]), .in1(SUM_REST[2]), .in2(SUM_REST[3]), .in3(SUM_REST[4]), .in4(SUM_REST[5]),
    .in5(SUM_REST[6]), .in6(SUM_REST[7]), .in7(SUM_REST[8]), .in8(SUM_REST[9]), .in9(1'b0), .in10(1'b0),
    .in11(1'b0), .in12(1'b0), .in13(1'b0), .in14(1'b0), .in15(1'b0), .out(DERECHA[1]), .sel(shiftR));
  Multiplexer #(.select(4)) multiplexer_10 (
    .in0(SUM_REST[0]), .in1(SUM_REST[1]), .in2(SUM_REST[2]), .in3(SUM_REST[3]), .in4(SUM_REST[4]),
    .in5(SUM_REST[5]), .in6(SUM_REST[6]), .in7(SUM_REST[7]), .in8(SUM_REST[8]), .in9(SUM_REST[9]),
    .in10(1'b0), .in11(1'b0), .in12(1'b0), .in13(1'b0), .in14(1'b0), .in15(1'b0), .out(DERECHA[0]),
    .sel(shiftR));
endmodule

module ALUFLAGS (
  input  Cout,
  input  [2:0] ALU_CONTROL,
  input  SUMARESTA9,
  input  A9,
  input  B9,
  input  [9:0] RESULTADO,
  output [3:0] FLAGS
);

  wire xnor_1_out, xor_1_out;

  xor xor_1 (xor_1_out, SUMARESTA9, A9);
  NotExactlyOne xnor_1 (.out(xnor_1_out), .in0(B9), .in1(A9), .in2(ALU_CONTROL[0]));
  and and_1 (FLAGS[1], Cout, ~ALU_CONTROL[2], ~ALU_CONTROL[1]);  // AND_Gate
  and and_2 (FLAGS[0], ~ALU_CONTROL[1], ~ALU_CONTROL[2], xor_1_out, ~xnor_1_out);  // AND_Gate
  and and_3 (FLAGS[2], ~RESULTADO[0], ~RESULTADO[1], ~RESULTADO[2], ~RESULTADO[3], ~RESULTADO[4], ~RESULTADO[5], ~RESULTADO[6], ~RESULTADO[7], ~RESULTADO[8], ~RESULTADO[9]);  // AND_Gate

  assign FLAGS[3] = RESULTADO[9];
endmodule
